# Fritzing sketch Schematics (saved by Fritzing 0.6.2b)
breadboards: 3

parts:
  J3 = Basic Servo
  J2 = Basic Servo
  J1 = Basic Servo
  J5 = Basic Servo
  J6 = Basic Servo
  J7 = Basic Servo
  J4 = Basic Servo
  J8 = Basic Servo
  IC1 = ULN2003A [package="DIP16 [THT]"]
  U1 = Arduino Mega
  J10 = screw terminal, 4 pins
  U2 = Voltage Regulator - 5V [package="TO220 [THT]"]
  DC_Power2 = DC Power [voltage=12]

nets:
  GND: J3.gnd, J2.gnd, J1.gnd, J5.gnd, J6.gnd, J7.gnd, J4.gnd, J8.gnd, IC1.0V, U1.GND, J10.pin1, U2.GND, DC_Power2.GND
  VCC: J3.vcc, J2.vcc, J1.vcc, J5.vcc, J6.vcc, J7.vcc, J4.vcc, J8.vcc, U2.output_voltage
  N1: J3.pulse, U1.D7
  N2: J2.pulse, U1.D6
  N3: J1.pulse, U1.D5
  N4: J5.pulse, U1.D9
  N5: J6.pulse, U1.D10
  N6: J7.pulse, U1.D11
  N7: J4.pulse, U1.D8
  N8: J8.pulse, U1.D12
  N9: IC1.In_1, U1.D2
  N10: IC1.In_2, U1.D3
  N11: IC1.In_3, U1.D4
  N12: IC1.COM_-_Common, U1.VIN, U2.input_voltage, DC_Power2.V+
  N13: IC1.Out_3, J10.pin4
  N14: IC1.Out_2, J10.pin3
  N15: IC1.Out_1, J10.pin2

notes:
  Caipirinha Hero, Projeto para Open Call ADK do Google Developer Day 2011., 0.1
  Caipirinha Hero v0.1b
