# Fritzing sketch Schematics_5V (saved by Fritzing 0.6.2b)
breadboards: 3

parts:
  J3 = Basic Servo
  J2 = Basic Servo
  J1 = Basic Servo
  J5 = Basic Servo
  J6 = Basic Servo
  J7 = Basic Servo
  J4 = Basic Servo
  J8 = Basic Servo
  U1 = Arduino Mega
  DC_Power2 = DC Power [voltage=12]

nets:
  GND: J3.gnd, J2.gnd, J1.gnd, J5.gnd, J6.gnd, J7.gnd, J4.gnd, J8.gnd, U1.GND, DC_Power2.GND
  VCC: J3.vcc, J2.vcc, J1.vcc, J5.vcc, J6.vcc, J7.vcc, J4.vcc, J8.vcc, U1.VIN, DC_Power2.V+
  N1: J3.pulse, U1.D7
  N2: J2.pulse, U1.D6
  N3: J1.pulse, U1.D5
  N4: J5.pulse, U1.D9
  N5: J6.pulse, U1.D10
  N6: J7.pulse, U1.D11
  N7: J4.pulse, U1.D8
  N8: J8.pulse, U1.D12

notes:
  Caipirinha Hero, Projeto para Open Call ADK do Google Developer Day 2011., 0.1
  Caipirinha Hero v0.1 (5V)
  C.Hero 5V (bottom)
